# Fritzing sketch shybot (saved by Fritzing 0.9.3b)
breadboards: 1

parts:
  Componente1 = Arduino Uno (Rev3)  # not connected
  hc-sr1 = hc-sr04
  Componente3 = Arduino Motor Shield
  Componente2 = Ludus ProtoShield
  LED1 = smd LED [color="Green (570nm)" package="1206 [SMD]"]
  LED2 = smd LED [color="Red (633nm)" package="1206 [SMD]"]
  M1 = DC Motor
  M2 = DC Motor
  S1 = Pushbutton [package="[SMD]"]
  R1 = Resistor [tolerance=±5% resistance=1k package=THT]
  M3 = Dagu DGServo 9g (End View) [part_number=RS001B]

nets:
  VCC: hc-sr1.VCC, Componente2.PWR_RAIL, S1.Pin_1, S1.Pin_2, M3.vcc
  N1: hc-sr1.Trig, Componente2.PWMA
  N2: hc-sr1.Echo, Componente2.D2
  GND: hc-sr1.GND, Componente2.GND, LED1.cathode, LED1.anode, LED2.cathode, LED2.anode, R1.Pin_0, M3.gnd
  N3: Componente3.OUT3, M1.pin_1
  N4: Componente3.OUT4, M1.pin_2
  N5: Componente3.OUT2, M2.pin_1
  N6: Componente3.OUT1, M2.pin_2
  N7: Componente2.D0, M3.pulse
  N8: Componente2.D11, S1.Pin_3, S1.Pin_4, R1.Pin_1

notes:
  The shields are representative. I use one from keyestudio.
  The servo is connected with ultrasonic sensor
  Wheels
  Power On/Off button with Led indicator
